# Fritzing sketch rfidpi (saved by Fritzing 0.9.3b)
breadboards: 1

parts:
  RFID_Module = RFID RC522 SIP - 8 pins [chip_label="RFID RC522" package="SIP (Single Inline) [THT]"]
  Raspberry_Pi = Raspberry Pi 3 [part_number=RPI-3-V1.2]
  error_pin_14 = LED - 5mm [color="Red (633nm)" package="5 mm [THT]"]
  Check_out_pin_23 = LED - 5mm [color="Green (555nm)" package="5 mm [THT]"]
  proccessing_pin_15 = LED - 5mm [color="Yellow (574nm)" package="5 mm [THT]"]
  Check_in_pin_18 = LED - 5mm [color="Green (555nm)" package="5 mm [THT]"]
  R1 = Resistor [tolerance=±5% resistance=330 package="0603 [SMD]"]
  Busser_pin_24 = Piezo Speaker

nets:
  N1: RFID_Module.NSS, Raspberry_Pi.GPIO8
  N2: RFID_Module.SCK, Raspberry_Pi.GPIO11
  N3: RFID_Module.MOSI, Raspberry_Pi.GPIO10
  N4: RFID_Module.MISO, Raspberry_Pi.GPIO9
  GND: RFID_Module.GND, Raspberry_Pi.GND, R1.Pin_0, Busser_pin_24.pin1
  N5: RFID_Module.RST, Raspberry_Pi.GPIO25
  3V3: RFID_Module.VCC, Raspberry_Pi.3v3, Raspberry_Pi.3V3
  N6: Raspberry_Pi.GPIO24, Busser_pin_24.pin2
  N7: Raspberry_Pi.GPIO23, Check_out_pin_23.anode
  N8: Raspberry_Pi.GPIO18, Check_in_pin_18.anode
  N9: Raspberry_Pi.GPIO15, proccessing_pin_15.anode
  N10: Raspberry_Pi.GPIO14, error_pin_14.anode
  N11: error_pin_14.cathode, Check_out_pin_23.cathode, proccessing_pin_15.cathode, Check_in_pin_18.cathode, R1.Pin_1

custom parts:
  RFID RC522 SIP - 8 pins: A SIP stand-in part for RFID RC522 . With 8 pins on a 300 mil single inline package (SIP) footprint.
